// Logisim project CSE332 Project.circ as structural Verilog: 4 circuits, main circuit main
module main (
  input  Cin,
  input  MemToReg,
  input  R_I,
  input  R_I_2,
  input  R_I_3,
  input  SW,
  input  Select,
  input  LW,
  input  Clear,
  input  Clear_2,
  output [3:0] RT,
  output [4:0] Opcode,
  output [3:0] RD,
  output [3:0] RS,
  output [16:0] ALU_Result,
  output [16:0] Read_Data_2,
  output [16:0] Read_Data_1,
  output [1:0] OpCode_2
);

  wire Clock_out;
  wire [4:0] bit_extender_1_out, bit_extender_2_out, bit_extender_3_out, multiplexer_1_out;
  wire [16:0] adder_1_out, bit_extender_5_out, multiplexer_2_out, multiplexer_3_out, ram_1_data, register_1_q;

  Register #(.width(17)) register_1 (.D(adder_1_out), .Q(register_1_q), .clk(Clock_out), .clr(Clear_2));  // open: en
  Clock Clock (.out(Clock_out));
  Adder #(.width(17)) adder_1 (.a(register_1_q), .b(17'h1), .out(adder_1_out));  // open: cin, cout
  ROM #(.addrWidth(17), .dataWidth(17)) rom_1 (.addr(register_1_q), .data({Opcode, RS, RT, RD}));  // open: sel
  assign bit_extender_1_out = {{1{1'b0}}, RS};  // Bit_Extender bit_extender_1
  assign bit_extender_2_out = {{1{1'b0}}, RT};  // Bit_Extender bit_extender_2
  assign bit_extender_3_out = {{1{1'b0}}, RD};  // Bit_Extender bit_extender_3
  Bit_Extender #(.in_width(5), .out_width(2)) bit_extender_4 (.in(Opcode), .out(OpCode_2));
  assign bit_extender_5_out = {{13{1'b0}}, RD};  // Bit_Extender bit_extender_5
  Multiplexer #(.width(5), .enable("false")) multiplexer_1 (
    .in0(bit_extender_2_out), .in1(bit_extender_3_out), .out(multiplexer_1_out), .sel(R_I));
  _17_Bit_Register_File u_17_bit_register_file_1 (
    .Data_Write(multiplexer_3_out), .Clock(Clock_out), .Enable(R_I_2), .Data_Read_1(Read_Data_1),
    .Data_Read_2(Read_Data_2), .RD(multiplexer_1_out), .RS(bit_extender_1_out), .RT(bit_extender_2_out));
  Multiplexer #(.width(17), .enable("false")) multiplexer_2 (
    .in0(Read_Data_2), .in1(bit_extender_5_out), .out(multiplexer_2_out), .sel(R_I_3));
  _17_Bit_ALU u_17_bit_alu_1 (
    .B(multiplexer_2_out), .A(Read_Data_1), .OpCode(OpCode_2), .Cin(Cin), .Result(ALU_Result));  // open: OverFlow, Zero, Cout
  RAM #(.addrWidth(17), .dataWidth(17), .bus("separate")) ram_1 (
    .addr(ALU_Result), .din(Read_Data_2), .data(ram_1_data), .str(SW), .sel(Select), .clk(Clock_out),
    .ld(LW), .clr(Clear));
  Multiplexer #(.width(17), .enable("false")) multiplexer_3 (
    .in0(ALU_Result), .in1(ram_1_data), .out(multiplexer_3_out), .sel(MemToReg));

  // Notes on the sheet:
  //   Operation Code
  //   00  ADD
  //   10  X-nor
  //   Instruction Fetch
  //   Instruction Memory
  //   Instruction Fetch
  //   01  Multi
  //   11  Nor
  //   contents of rom_1 (hex, n*v repeats v):
  //   123 2241
  //   Instruction Decode
  //   RS
  //   RT
  //   RT/RD
  //   Opcode
  //   Instruction Decode
  //   Execute
  //   Write Data Line
  //   Execute
  //   Memory Access
  //   Access Memory
  //   Memory Access
  //   Write Back
  //   Write Back
endmodule

module _1_Bit_ALU (
  input  B,
  input  A,
  input  Cin,
  input  [1:0] OpCode,
  output Overflow,
  output Output,
  output Zero,
  output Cout
);

  wire adder_1_out, multiplier_1_out, nor_1_out, xnor_1_out;

  Adder #(.width(1)) adder_1 (.a(A), .b(B), .out(adder_1_out), .cin(Cin), .cout(Cout));
  Multiplier #(.width(1)) multiplier_1 (.a(A), .b(B), .out(multiplier_1_out), .cin(Cin));  // open: cout
  xnor xnor_1 (xnor_1_out, A, B);
  nor nor_1 (nor_1_out, A, B);
  Multiplexer #(.select(2), .enable("false")) multiplexer_1 (
    .in0(adder_1_out), .in1(multiplier_1_out), .in2(xnor_1_out), .in3(nor_1_out), .out(Output), .sel(OpCode));
  xor xor_1 (Overflow, Cout, Output);
  nor nor_2 (Zero, Output, Cout);
endmodule

module _17_Bit_Register_File (
  input  [16:0] Data_Write,
  input  Clock,
  input  [4:0] RS,
  input  Enable,
  input  [4:0] RD,
  input  [4:0] RT,
  output [16:0] Data_Read_1,
  output [16:0] Data_Read_2
);

  wire demultiplexer_1_out0, demultiplexer_1_out1, demultiplexer_1_out2, demultiplexer_1_out3,
       demultiplexer_1_out4, demultiplexer_1_out5, demultiplexer_1_out6, demultiplexer_1_out7,
       demultiplexer_1_out8, demultiplexer_1_out9, demultiplexer_1_out10, demultiplexer_1_out11,
       demultiplexer_1_out12, demultiplexer_1_out13, demultiplexer_1_out14, demultiplexer_1_out15,
       demultiplexer_1_out16, Reset_out;
  wire [16:0] register_1_q, register_2_q, register_3_q, register_4_q, register_5_q, register_6_q,
       register_7_q, register_8_q, register_9_q, register_10_q, register_11_q, register_12_q, register_13_q,
       register_14_q, register_15_q, register_16_q, register_17_q;

  Demultiplexer #(.select(5), .enable("false")) demultiplexer_1 (
    .out0(demultiplexer_1_out0), .out1(demultiplexer_1_out1), .out2(demultiplexer_1_out2),
    .out3(demultiplexer_1_out3), .out4(demultiplexer_1_out4), .out5(demultiplexer_1_out5),
    .out6(demultiplexer_1_out6), .out7(demultiplexer_1_out7), .out8(demultiplexer_1_out8),
    .out9(demultiplexer_1_out9), .out10(demultiplexer_1_out10), .out11(demultiplexer_1_out11),
    .out12(demultiplexer_1_out12), .out13(demultiplexer_1_out13), .out14(demultiplexer_1_out14),
    .out15(demultiplexer_1_out15), .out16(demultiplexer_1_out16), .in(Enable), .sel(RD));  // open: out17, out18, out19, out20, out21, out22, out23, out24, out25, out26, out27, out28, out29, out30, out31
  Register #(.width(17)) register_1 (
    .D(Data_Write), .en(demultiplexer_1_out0), .Q(register_1_q), .clk(Clock), .clr(Reset_out));
  Register #(.width(17)) register_2 (
    .D(Data_Write), .en(demultiplexer_1_out1), .Q(register_2_q), .clk(Clock), .clr(Reset_out));
  Register #(.width(17)) register_3 (
    .D(Data_Write), .en(demultiplexer_1_out2), .Q(register_3_q), .clk(Clock), .clr(Reset_out));
  Register #(.width(17)) register_4 (
    .D(Data_Write), .en(demultiplexer_1_out3), .Q(register_4_q), .clk(Clock), .clr(Reset_out));
  Register #(.width(17)) register_5 (
    .D(Data_Write), .en(demultiplexer_1_out4), .Q(register_5_q), .clk(Clock), .clr(Reset_out));
  Register #(.width(17)) register_6 (
    .D(Data_Write), .en(demultiplexer_1_out5), .Q(register_6_q), .clk(Clock), .clr(Reset_out));
  Register #(.width(17)) register_7 (
    .D(Data_Write), .en(demultiplexer_1_out6), .Q(register_7_q), .clk(Clock), .clr(Reset_out));
  Register #(.width(17)) register_8 (
    .D(Data_Write), .en(demultiplexer_1_out7), .Q(register_8_q), .clk(Clock), .clr(Reset_out));
  Register #(.width(17)) register_9 (
    .D(Data_Write), .en(demultiplexer_1_out8), .Q(register_9_q), .clk(Clock), .clr(Reset_out));
  Register #(.width(17)) register_10 (
    .D(Data_Write), .en(demultiplexer_1_out9), .Q(register_10_q), .clk(Clock), .clr(Reset_out));
  Register #(.width(17)) register_11 (
    .D(Data_Write), .en(demultiplexer_1_out10), .Q(register_11_q), .clk(Clock), .clr(Reset_out));
  Register #(.width(17)) register_12 (
    .D(Data_Write), .en(demultiplexer_1_out11), .Q(register_12_q), .clk(Clock), .clr(Reset_out));
  Register #(.width(17)) register_13 (
    .D(Data_Write), .en(demultiplexer_1_out12), .Q(register_13_q), .clk(Clock), .clr(Reset_out));
  Register #(.width(17)) register_14 (
    .D(Data_Write), .en(demultiplexer_1_out13), .Q(register_14_q), .clk(Clock), .clr(Reset_out));
  Register #(.width(17)) register_15 (
    .D(Data_Write), .en(demultiplexer_1_out14), .Q(register_15_q), .clk(Clock), .clr(Reset_out));
  Register #(.width(17)) register_16 (
    .D(Data_Write), .en(demultiplexer_1_out15), .Q(register_16_q), .clk(Clock), .clr(Reset_out));
  Register #(.width(17)) register_17 (
    .D(Data_Write), .en(demultiplexer_1_out16), .Q(register_17_q), .clk(Clock), .clr(Reset_out));
  Button Reset (.out(Reset_out));
  Multiplexer #(.select(5), .width(17), .enable("false")) multiplexer_1 (
    .in0(register_1_q), .in1(register_2_q), .in2(register_3_q), .in3(register_4_q), .in4(register_5_q),
    .in5(register_6_q), .in6(register_7_q), .in7(register_8_q), .in8(register_9_q), .in9(register_10_q),
    .in10(register_11_q), .in11(register_12_q), .in12(register_13_q), .in13(register_14_q),
    .in14(register_15_q), .in15(register_16_q), .in16(register_17_q), .out(Data_Read_1), .sel(RS));  // open: in17, in18, in19, in20, in21, in22, in23, in24, in25, in26, in27, in28, in29, in30, in31
  Multiplexer #(.select(5), .width(17), .enable("false")) multiplexer_2 (
    .in0(register_1_q), .in1(register_2_q), .in2(register_3_q), .in3(register_4_q), .in4(register_5_q),
    .in5(register_6_q), .in6(register_7_q), .in7(register_8_q), .in8(register_9_q), .in9(register_10_q),
    .in10(register_11_q), .in11(register_12_q), .in12(register_13_q), .in13(register_14_q),
    .in14(register_15_q), .in15(register_16_q), .in16(register_17_q), .out(Data_Read_2), .sel(RT));  // open: in17, in18, in19, in20, in21, in22, in23, in24, in25, in26, in27, in28, in29, in30, in31
endmodule

module _17_Bit_ALU (
  input  [1:0] OpCode,
  input  Cin,
  input  [16:0] B,
  input  [16:0] A,
  output Cout,
  output [16:0] Result,
  output [16:0] OverFlow,
  output [16:0] Zero
);

  wire n1_bit_alu_1_cout, n1_bit_alu_2_cout, n1_bit_alu_3_cout, n1_bit_alu_4_cout, n1_bit_alu_5_cout,
       n1_bit_alu_6_cout, n1_bit_alu_7_cout, n1_bit_alu_8_cout, n1_bit_alu_9_cout, n1_bit_alu_10_cout,
       n1_bit_alu_11_cout, n1_bit_alu_12_cout, n1_bit_alu_13_cout, n1_bit_alu_14_cout, n1_bit_alu_15_cout,
       n1_bit_alu_16_cout;

  _1_Bit_ALU u_1_bit_alu_1 (
    .Overflow(OverFlow[0]), .Output(Result[0]), .Zero(Zero[0]), .Cout(n1_bit_alu_1_cout), .B(B[0]), .A(A[0]),
    .Cin(Cin), .OpCode(OpCode));
  _1_Bit_ALU u_1_bit_alu_2 (
    .Overflow(OverFlow[1]), .Output(Result[1]), .Zero(Zero[1]), .Cout(n1_bit_alu_2_cout), .B(B[1]), .A(A[1]),
    .Cin(n1_bit_alu_1_cout), .OpCode(OpCode));
  _1_Bit_ALU u_1_bit_alu_3 (
    .Overflow(OverFlow[2]), .Output(Result[2]), .Zero(Zero[2]), .Cout(n1_bit_alu_3_cout), .B(B[2]), .A(A[2]),
    .Cin(n1_bit_alu_2_cout), .OpCode(OpCode));
  _1_Bit_ALU u_1_bit_alu_4 (
    .Overflow(OverFlow[3]), .Output(Result[3]), .Zero(Zero[3]), .Cout(n1_bit_alu_4_cout), .B(B[3]), .A(A[3]),
    .Cin(n1_bit_alu_3_cout), .OpCode(OpCode));
  _1_Bit_ALU u_1_bit_alu_5 (
    .Overflow(OverFlow[4]), .Output(Result[4]), .Zero(Zero[4]), .Cout(n1_bit_alu_5_cout), .B(B[4]), .A(A[4]),
    .Cin(n1_bit_alu_4_cout), .OpCode(OpCode));
  _1_Bit_ALU u_1_bit_alu_6 (
    .Overflow(OverFlow[5]), .Output(Result[5]), .Zero(Zero[5]), .Cout(n1_bit_alu_6_cout), .B(B[5]), .A(A[5]),
    .Cin(n1_bit_alu_5_cout), .OpCode(OpCode));
  _1_Bit_ALU u_1_bit_alu_7 (
    .Overflow(OverFlow[6]), .Output(Result[6]), .Zero(Zero[6]), .Cout(n1_bit_alu_7_cout), .B(B[6]), .A(A[6]),
    .Cin(n1_bit_alu_6_cout), .OpCode(OpCode));
  _1_Bit_ALU u_1_bit_alu_8 (
    .Overflow(OverFlow[7]), .Output(Result[7]), .Zero(Zero[7]), .Cout(n1_bit_alu_8_cout), .B(B[7]), .A(A[7]),
    .Cin(n1_bit_alu_7_cout), .OpCode(OpCode));
  _1_Bit_ALU u_1_bit_alu_9 (
    .Overflow(OverFlow[8]), .Output(Result[8]), .Zero(Zero[8]), .Cout(n1_bit_alu_9_cout), .B(B[8]), .A(A[8]),
    .Cin(n1_bit_alu_8_cout), .OpCode(OpCode));
  _1_Bit_ALU u_1_bit_alu_10 (
    .Overflow(OverFlow[9]), .Output(Result[9]), .Zero(Zero[9]), .Cout(n1_bit_alu_10_cout), .B(B[9]),
    .A(A[9]), .Cin(n1_bit_alu_9_cout), .OpCode(OpCode));
  _1_Bit_ALU u_1_bit_alu_11 (
    .Overflow(OverFlow[10]), .Output(Result[10]), .Zero(Zero[10]), .Cout(n1_bit_alu_11_cout), .B(B[10]),
    .A(A[10]), .Cin(n1_bit_alu_10_cout), .OpCode(OpCode));
  _1_Bit_ALU u_1_bit_alu_12 (
    .Overflow(OverFlow[11]), .Output(Result[11]), .Zero(Zero[11]), .Cout(n1_bit_alu_12_cout), .B(B[11]),
    .A(A[11]), .Cin(n1_bit_alu_11_cout), .OpCode(OpCode));
  _1_Bit_ALU u_1_bit_alu_13 (
    .Overflow(OverFlow[12]), .Output(Result[12]), .Zero(Zero[12]), .Cout(n1_bit_alu_13_cout), .B(B[12]),
    .A(A[12]), .Cin(n1_bit_alu_12_cout), .OpCode(OpCode));
  _1_Bit_ALU u_1_bit_alu_14 (
    .Overflow(OverFlow[13]), .Output(Result[13]), .Zero(Zero[13]), .Cout(n1_bit_alu_14_cout), .B(B[13]),
    .A(A[13]), .Cin(n1_bit_alu_13_cout), .OpCode(OpCode));
  _1_Bit_ALU u_1_bit_alu_15 (
    .Overflow(OverFlow[14]), .Output(Result[14]), .Zero(Zero[14]), .Cout(n1_bit_alu_15_cout), .B(B[14]),
    .A(A[14]), .Cin(n1_bit_alu_14_cout), .OpCode(OpCode));
  _1_Bit_ALU u_1_bit_alu_16 (
    .Overflow(OverFlow[15]), .Output(Result[15]), .Zero(Zero[15]), .Cout(n1_bit_alu_16_cout), .B(B[15]),
    .A(A[15]), .Cin(n1_bit_alu_15_cout), .OpCode(OpCode));
  _1_Bit_ALU u_1_bit_alu_17 (
    .Overflow(OverFlow[16]), .Output(Result[16]), .Zero(Zero[16]), .Cout(Cout), .B(B[16]), .A(A[16]),
    .Cin(n1_bit_alu_16_cout), .OpCode(OpCode));
endmodule
