// Logisim project 2-Bit Logic Unit.circ as structural Verilog: 2 circuits, main circuit main
// Main
module main (
  input  B2,
  input  B1,
  input  A2,
  input  A1,
  input  [1:0] S1_S2,
  output [1:0] F2_F1
);

  _2_Bit_Logic_Unit u_2_bit_logic_unit_1 (
    .S1_S2(S1_S2), .A1(A1), .A2(A2), .B1(B1), .B2(B2), .F2_F1(F2_F1));  // open: F1, F2
endmodule

// 2 Bit Logic Unit
module _2_Bit_Logic_Unit (
  input  A1,
  input  B1,
  input  A2,
  input  B2,
  input  [1:0] S1_S2,
  output F1,
  output [1:0] F2_F1,
  output F2
);

  wire and_1_out, and_2_out, not_1_out, not_2_out, or_1_out, or_2_out, xor_1_out, xor_2_out;

  and and_1 (and_1_out, A1, B1);
  or or_1 (or_1_out, A1, B1);
  xor xor_1 (xor_1_out, A1, B1);
  not not_1 (not_1_out, A1);
  and and_2 (and_2_out, A2, B2);
  or or_2 (or_2_out, A2, B2);
  xor xor_2 (xor_2_out, A2, B2);
  not not_2 (not_2_out, A2);
  Multiplexer #(.select(2), .enable("false")) multiplexer_1 (
    .in0(and_1_out), .in1(or_1_out), .in2(xor_1_out), .in3(not_1_out), .out(F1), .sel(S1_S2));
  Multiplexer #(.select(2), .enable("false")) multiplexer_2 (
    .in0(and_2_out), .in1(or_2_out), .in2(xor_2_out), .in3(not_2_out), .out(F2), .sel(S1_S2));

  assign F2_F1 = {F2, F1};

  // Notes on the sheet:
  //   SELECTORS
endmodule
