// Logisim project 4-Bit Arithmetic Unit.circ as structural Verilog: 2 circuits, main circuit 4-Bit Arithmetic Unit
module main (
  input  [1:0] Selection_Inputs_S1_S0,
  input  Cin,
  input  A0,
  input  B0,
  input  A1,
  input  B1,
  input  A2,
  input  B2,
  input  A3,
  input  B3,
  input  in_11,
  output [3:0] D3_D2_D1_D0,
  output Cout
);

  _4_Bit_Arithmetic_Unit u_4_bit_arithmetic_unit_1 (
    .Cin(Cin), .A0(A0), .B0(B0), .A1(A1), .B1(B1), .A2(A2), .B2(B2), .A3(A3), .B3(B3), .in_11(in_11),
    .S1_S0(Selection_Inputs_S1_S0), .D3_D2_D1_D0(D3_D2_D1_D0), .Cout(Cout));
endmodule

module _4_Bit_Arithmetic_Unit (
  input  Cin,
  input  A0,
  input  [1:0] S1_S0,
  input  B0,
  input  A1,
  input  B1,
  input  A2,
  input  B2,
  input  A3,
  input  B3,
  input  in_11,
  output [3:0] D3_D2_D1_D0,
  output Cout
);

  wire adder_1_cout, adder_2_cout, adder_3_cout, multiplexer_1_out, multiplexer_2_out, multiplexer_3_out,
       multiplexer_4_out, not_1_out, not_2_out, not_3_out, not_4_out, not_5_out;

  not not_1 (not_1_out, B0);
  not not_2 (not_2_out, B1);
  not not_3 (not_3_out, B2);
  not not_4 (not_4_out, B3);
  not not_5 (not_5_out, in_11);
  Multiplexer #(.select(2), .enable("false")) multiplexer_1 (
    .in0(B0), .in1(not_1_out), .in2(in_11), .in3(not_5_out), .out(multiplexer_1_out), .sel(S1_S0));
  Multiplexer #(.select(2), .enable("false")) multiplexer_2 (
    .in0(B1), .in1(not_2_out), .in2(in_11), .in3(not_5_out), .out(multiplexer_2_out), .sel(S1_S0));
  Multiplexer #(.select(2), .enable("false")) multiplexer_3 (
    .in0(B2), .in1(not_3_out), .in2(in_11), .in3(not_5_out), .out(multiplexer_3_out), .sel(S1_S0));
  Multiplexer #(.select(2), .enable("false")) multiplexer_4 (
    .in0(B3), .in1(not_4_out), .in2(in_11), .in3(not_5_out), .out(multiplexer_4_out), .sel(S1_S0));
  Adder #(.width(1)) adder_1 (.a(A0), .b(multiplexer_1_out), .out(D3_D2_D1_D0[0]), .cin(Cin), .cout(adder_1_cout));
  Adder #(.width(1)) adder_2 (
    .a(A1), .b(multiplexer_2_out), .out(D3_D2_D1_D0[1]), .cin(adder_1_cout), .cout(adder_2_cout));
  Adder #(.width(1)) adder_3 (
    .a(A2), .b(multiplexer_3_out), .out(D3_D2_D1_D0[2]), .cin(adder_2_cout), .cout(adder_3_cout));
  Adder #(.width(1)) adder_4 (.a(A3), .b(multiplexer_4_out), .out(D3_D2_D1_D0[3]), .cin(adder_3_cout), .cout(Cout));
endmodule
