// Logisim project 4 Bit Binary Multiplication Unit.circ as structural Verilog: 3 circuits, main circuit main
module main (
  input  A0,
  input  B3,
  input  A1,
  input  B2,
  input  A2,
  input  B1,
  input  A3,
  input  B0,
  input  in_9,
  output S7,
  output S6,
  output S5,
  output S4,
  output S3,
  output S2,
  output S1,
  output S0
);

  _4_Bit_Binary_Multiplication_Unit u_4_bit_binary_multiplication_unit_1 (
    .A3(A3), .A2(A2), .A1(A1), .A0(A0), .B3(B3), .B2(B2), .B1(B1), .B0(B0), .S7(S7), .S6(S6), .S5(S5),
    .S4(S4), .S3(S3), .S2(S2), .S1(S1), .S0(S0), .in_9(in_9), .in_10(in_9));
endmodule

module _4_Bit_Adder (
  input  Cin,
  input  A0,
  input  B0,
  input  A1,
  input  B1,
  input  A2,
  input  B2,
  input  A3,
  input  B3,
  output S0,
  output S1,
  output S2,
  output S3,
  output Cout
);

  wire adder_1_cout, adder_2_cout, adder_3_cout;

  Adder #(.width(1)) adder_1 (.a(A0), .b(B0), .out(S0), .cin(Cin), .cout(adder_1_cout));
  Adder #(.width(1)) adder_2 (.a(A1), .b(B1), .out(S1), .cin(adder_1_cout), .cout(adder_2_cout));
  Adder #(.width(1)) adder_3 (.a(A2), .b(B2), .out(S2), .cin(adder_2_cout), .cout(adder_3_cout));
  Adder #(.width(1)) adder_4 (.a(A3), .b(B3), .out(S3), .cin(adder_3_cout), .cout(Cout));
endmodule

module _4_Bit_Binary_Multiplication_Unit (
  input  A1,
  input  A0,
  input  B3,
  input  B2,
  input  B1,
  input  B0,
  input  A3,
  input  A2,
  input  in_9,
  input  in_10,
  output S7,
  output S6,
  output S5,
  output S4,
  output S3,
  output S2,
  output S1,
  output S0
);

  wire and_1_out, and_2_out, and_3_out, and_4_out, and_5_out, and_6_out, and_7_out, and_8_out, and_9_out,
       and_10_out, and_11_out, and_12_out, and_13_out, and_14_out, and_15_out, n4_bit_adder_2_cout,
       n4_bit_adder_2_s1, n4_bit_adder_2_s2, n4_bit_adder_2_s3, n4_bit_adder_3_cout, n4_bit_adder_3_s1,
       n4_bit_adder_3_s2, n4_bit_adder_3_s3;

  and and_1 (and_1_out, A3, B3);
  and and_2 (and_2_out, A3, B2);
  and and_3 (and_3_out, A3, B1);
  and and_4 (and_4_out, A2, B2);
  and and_5 (and_5_out, A2, B3);
  and and_6 (and_6_out, A3, B0);
  and and_7 (and_7_out, A2, B1);
  _4_Bit_Adder u_4_bit_adder_1 (
    .A0(n4_bit_adder_2_s1), .B0(and_6_out), .A1(n4_bit_adder_2_s2), .B1(and_3_out), .A2(n4_bit_adder_2_s3),
    .B2(and_2_out), .A3(in_9), .B3(and_1_out), .Cin(n4_bit_adder_2_cout), .Cout(S7), .S0(S3), .S1(S4),
    .S2(S5), .S3(S6));
  and and_8 (and_8_out, A2, B0);
  and and_9 (and_9_out, A1, B3);
  and and_10 (and_10_out, A1, B2);
  _4_Bit_Adder u_4_bit_adder_2 (
    .A0(n4_bit_adder_3_s1), .B0(and_8_out), .A1(n4_bit_adder_3_s2), .B1(and_7_out), .A2(n4_bit_adder_3_s3),
    .B2(and_4_out), .A3(and_5_out), .B3(in_9), .Cin(n4_bit_adder_3_cout), .Cout(n4_bit_adder_2_cout),
    .S0(S2), .S1(n4_bit_adder_2_s1), .S2(n4_bit_adder_2_s2), .S3(n4_bit_adder_2_s3));
  and and_11 (and_11_out, A1, B1);
  and and_12 (and_12_out, A1, B0);
  and and_13 (and_13_out, A0, B3);
  _4_Bit_Adder u_4_bit_adder_3 (
    .A0(and_12_out), .B0(and_15_out), .A1(and_11_out), .B1(and_14_out), .A2(and_13_out), .B2(and_10_out),
    .A3(and_9_out), .B3(in_9), .Cin(in_10), .Cout(n4_bit_adder_3_cout), .S0(S1), .S1(n4_bit_adder_3_s1),
    .S2(n4_bit_adder_3_s2), .S3(n4_bit_adder_3_s3));
  and and_14 (and_14_out, A0, B2);
  and and_15 (and_15_out, A0, B1);
  and and_16 (S0, A0, B0);
endmodule
