// Logisim project 4 Bit Universal Shift Register.circ as structural Verilog: 2 circuits, main circuit main
module main (
  input  [1:0] S1_S0,
  input  Shift_Right,
  input  I3,
  input  I2,
  input  I1,
  input  Shift_Left,
  input  I0,
  output A3,
  output A2,
  output A1,
  output A0
);

  _4_Bit_USR u_4_bit_usr_1 (
    .Input_for_Shift_right(Shift_Right), .I3(I3), .I2(I2), .I1(I1), .Input_for_Shift_left(Shift_Left),
    .I0(I0), .S1_S0(S1_S0), .A3(A3), .A2(A2), .A1(A1), .A0(A0));
endmodule

module _4_Bit_USR (
  input  [1:0] S1_S0,
  input  Input_for_Shift_right,
  input  I3,
  input  I2,
  input  I1,
  input  Input_for_Shift_left,
  input  I0,
  output A3,
  output A2,
  output A1,
  output A0
);

  wire Clear_out, Clock_out, multiplexer_1_out, multiplexer_2_out, multiplexer_3_out, multiplexer_4_out;

  Multiplexer #(.select(2), .enable("false")) multiplexer_1 (
    .in0(A3), .in1(Input_for_Shift_right), .in2(A2), .in3(I3), .out(multiplexer_1_out), .sel(S1_S0));
  Multiplexer #(.select(2), .enable("false")) multiplexer_2 (
    .in0(A2), .in1(A3), .in2(A1), .in3(I2), .out(multiplexer_2_out), .sel(S1_S0));
  Multiplexer #(.select(2), .enable("false")) multiplexer_3 (
    .in0(A1), .in1(A2), .in2(A0), .in3(I1), .out(multiplexer_3_out), .sel(S1_S0));
  Multiplexer #(.select(2), .enable("false")) multiplexer_4 (
    .in0(A0), .in1(A1), .in2(Input_for_Shift_left), .in3(I0), .out(multiplexer_4_out), .sel(S1_S0));
  Clock Clock (.out(Clock_out));
  D_Flip_Flop d_ff_1 (.clk(Clock_out), .D(multiplexer_1_out), .Q(A3), .reset(Clear_out));  // open: Qn, preset, en
  D_Flip_Flop d_ff_2 (.clk(Clock_out), .D(multiplexer_2_out), .Q(A2), .reset(Clear_out));  // open: Qn, preset, en
  D_Flip_Flop d_ff_3 (.clk(Clock_out), .D(multiplexer_3_out), .Q(A1), .reset(Clear_out));  // open: Qn, preset, en
  D_Flip_Flop d_ff_4 (.clk(Clock_out), .D(multiplexer_4_out), .Q(A0), .reset(Clear_out));  // open: Qn, preset, en
  Button Clear (.out(Clear_out));
endmodule
