// Logisim project 3 Bit Up Down Counter.circ as structural Verilog: 1 circuit, main circuit main
module main (
  input  M,
  input  in_2,
  input  Enable_Pin,
  output A,
  output B,
  output C
);

  wire and_1_out, and_2_out, and_3_out, and_4_out, Clock_out, not_1_out, or_1_out, or_2_out, Reset_out,
       TB_qn, TC_qn;

  Clock Clock (.out(Clock_out));
  Button Reset (.out(Reset_out));
  not not_1 (not_1_out, M);
  and and_1 (and_1_out, not_1_out, B, C);
  or or_1 (or_1_out, and_1_out, and_2_out);
  and and_2 (and_2_out, M, TB_qn, TC_qn);
  and and_3 (and_3_out, not_1_out, C);
  T_Flip_Flop TA (.clk(Clock_out), .T(or_1_out), .Q(A), .reset(Reset_out), .en(Enable_Pin));  // open: Qn, preset
  and and_4 (and_4_out, M, TC_qn);
  or or_2 (or_2_out, and_3_out, and_4_out);
  T_Flip_Flop TB (
    .clk(Clock_out), .T(or_2_out), .Q(B), .Qn(TB_qn), .reset(Reset_out), .en(Enable_Pin));  // open: preset
  T_Flip_Flop TC (.clk(Clock_out), .T(in_2), .Q(C), .Qn(TC_qn), .reset(Reset_out), .en(Enable_Pin));  // open: preset
endmodule
