// Logisim project 2 Bit Register File.circ as structural Verilog: 1 circuit, main circuit main
module main (
  input  [1:0] Input,
  input  [1:0] S1_S0,
  input  Demux,
  input  [1:0] S1_S0_2,
  input  [1:0] S1_S0_3,
  output [1:0] Output,
  output [1:0] Output_2
);

  wire Clock_out, demultiplexer_1_out0, demultiplexer_1_out1, demultiplexer_1_out2, demultiplexer_1_out3,
       Reset_out;
  wire [1:0] register_1_q, register_2_q, register_3_q, register_4_q;

  Demultiplexer #(.select(2), .enable("false")) demultiplexer_1 (
    .out0(demultiplexer_1_out0), .out1(demultiplexer_1_out1), .out2(demultiplexer_1_out2),
    .out3(demultiplexer_1_out3), .in(Demux), .sel(S1_S0_2));
  Clock Clock (.out(Clock_out));
  Register #(.width(2)) register_1 (
    .D(Input), .en(demultiplexer_1_out0), .Q(register_1_q), .clk(Clock_out), .clr(Reset_out));
  Register #(.width(2)) register_2 (
    .D(Input), .en(demultiplexer_1_out1), .Q(register_2_q), .clk(Clock_out));  // open: clr
  Register #(.width(2)) register_3 (
    .D(Input), .en(demultiplexer_1_out2), .Q(register_3_q), .clk(Clock_out));  // open: clr
  Register #(.width(2)) register_4 (
    .D(Input), .en(demultiplexer_1_out3), .Q(register_4_q), .clk(Clock_out), .clr(Reset_out));
  Button Reset (.out(Reset_out));
  Multiplexer #(.select(2), .width(2), .enable("false")) multiplexer_1 (
    .in0(register_1_q), .in1(register_2_q), .in2(register_3_q), .in3(register_4_q), .out(Output), .sel(S1_S0));
  Multiplexer #(.select(2), .width(2), .enable("false")) multiplexer_2 (
    .in0(register_1_q), .in1(register_2_q), .in2(register_3_q), .in3(register_4_q), .out(Output_2),
    .sel(S1_S0_3));
endmodule
