// Logisim project 16 Bit Arithmetic Logic Unit.circ as structural Verilog: 3 circuits, main circuit main
module main (
  input  Cin,
  input  Sub,
  input  B,
  input  A,
  input  [2:0] Op_Code,
  output Output,
  output Cout
);

  wire adder_1_out, and_1_out, comparator_1_eq, comparator_1_gt, comparator_1_lt, multiplier_1_out, or_1_out,
       xor_1_out, xor_2_out;

  xor xor_1 (xor_1_out, B, Sub);
  and and_1 (and_1_out, A, B);
  or or_1 (or_1_out, A, B);
  xor xor_2 (xor_2_out, A, B);
  Adder #(.width(1)) adder_1 (.a(A), .b(xor_1_out), .out(adder_1_out), .cin(Cin), .cout(Cout));
  Multiplier #(.width(1)) multiplier_1 (.a(A), .b(B), .out(multiplier_1_out), .cin(Cin));  // open: cout
  Comparator #(.width(1)) comparator_1 (.a(A), .b(B), .gt(comparator_1_gt), .eq(comparator_1_eq), .lt(comparator_1_lt));
  Multiplexer #(.select(3), .enable("false")) multiplexer_1 (
    .in0(and_1_out), .in1(or_1_out), .in2(xor_2_out), .in3(adder_1_out), .in4(multiplier_1_out),
    .in5(comparator_1_gt), .in6(comparator_1_eq), .in7(comparator_1_lt), .out(Output), .sel(Op_Code));
endmodule

module _16_Bit_ALU (
  input  [15:0] B,
  input  [15:0] A,
  input  Sub,
  input  Cin,
  input  [2:0] Op_Code,
  output [15:0] Ouput,
  output Cout
);

  wire main_1_cout, main_2_cout, main_3_cout, main_4_cout, main_5_cout, main_6_cout, main_7_cout,
       main_8_cout, main_9_cout, main_10_cout, main_11_cout, main_12_cout, main_13_cout, main_14_cout,
       main_15_cout;

  main main_1 (.Output(Ouput[0]), .Cout(main_1_cout), .Cin(Cin), .Sub(Sub), .B(B[0]), .A(A[0]), .Op_Code(Op_Code));
  main main_2 (
    .Output(Ouput[1]), .Cout(main_2_cout), .Cin(main_1_cout), .Sub(Sub), .B(B[1]), .A(A[1]), .Op_Code(Op_Code));
  main main_3 (
    .Output(Ouput[2]), .Cout(main_3_cout), .Cin(main_2_cout), .Sub(Sub), .B(B[2]), .A(A[2]), .Op_Code(Op_Code));
  main main_4 (
    .Output(Ouput[3]), .Cout(main_4_cout), .Cin(main_3_cout), .Sub(Sub), .B(B[3]), .A(A[3]), .Op_Code(Op_Code));
  main main_5 (
    .Output(Ouput[4]), .Cout(main_5_cout), .Cin(main_4_cout), .Sub(Sub), .B(B[4]), .A(A[4]), .Op_Code(Op_Code));
  main main_6 (
    .Output(Ouput[5]), .Cout(main_6_cout), .Cin(main_5_cout), .Sub(Sub), .B(B[5]), .A(A[5]), .Op_Code(Op_Code));
  main main_7 (
    .Output(Ouput[6]), .Cout(main_7_cout), .Cin(main_6_cout), .Sub(Sub), .B(B[6]), .A(A[6]), .Op_Code(Op_Code));
  main main_8 (
    .Output(Ouput[7]), .Cout(main_8_cout), .Cin(main_7_cout), .Sub(Sub), .B(B[7]), .A(A[7]), .Op_Code(Op_Code));
  main main_9 (
    .Output(Ouput[8]), .Cout(main_9_cout), .Cin(main_8_cout), .Sub(Sub), .B(B[8]), .A(A[8]), .Op_Code(Op_Code));
  main main_10 (
    .Output(Ouput[9]), .Cout(main_10_cout), .Cin(main_9_cout), .Sub(Sub), .B(A[9]), .A(B[9]),
    .Op_Code(Op_Code));
  main main_11 (
    .Output(Ouput[10]), .Cout(main_11_cout), .Cin(main_10_cout), .Sub(Sub), .B(B[10]), .A(A[10]),
    .Op_Code(Op_Code));
  main main_12 (
    .Output(Ouput[11]), .Cout(main_12_cout), .Cin(main_11_cout), .Sub(Sub), .B(B[11]), .A(A[11]),
    .Op_Code(Op_Code));
  main main_13 (
    .Output(Ouput[12]), .Cout(main_13_cout), .Cin(main_12_cout), .Sub(Sub), .B(B[12]), .A(A[12]),
    .Op_Code(Op_Code));
  main main_14 (
    .Output(Ouput[13]), .Cout(main_14_cout), .Cin(main_13_cout), .Sub(Sub), .B(B[13]), .A(A[13]),
    .Op_Code(Op_Code));
  main main_15 (
    .Output(Ouput[14]), .Cout(main_15_cout), .Cin(main_14_cout), .Sub(Sub), .B(B[14]), .A(A[14]),
    .Op_Code(Op_Code));
  main main_16 (
    .Output(Ouput[15]), .Cout(Cout), .Cin(main_15_cout), .Sub(Sub), .B(B[15]), .A(A[15]), .Op_Code(Op_Code));
endmodule

module _2Bit (
  input  Cin,
  input  Sub,
  input  [2:0] in_3,
  input  [1:0] A,
  input  [1:0] B,
  output [1:0] out_6,
  output Cout
);

  wire main_1_cout;

  main main_1 (.Output(out_6[0]), .Cout(main_1_cout), .Cin(Cin), .Sub(Sub), .B(B[0]), .A(A[0]), .Op_Code(in_3));
  main main_2 (.Output(out_6[1]), .Cout(Cout), .Cin(main_1_cout), .Sub(Sub), .B(B[1]), .A(A[1]), .Op_Code(in_3));
endmodule
