// Logisim project Lab 8.circ as structural Verilog: 4 circuits, main circuit main
module main (
  input  Cin,
  input  R_I,
  input  R_I_2,
  input  R_I_3,
  input  SW,
  input  Select,
  input  LW,
  input  Clear,
  input  in_9,
  input  Clear_2,
  output [15:0] out_11,
  output [3:0] RT,
  output [3:0] RS,
  output [15:0] out_14,
  output [15:0] ALU_Result,
  output [3:0] RD,
  output [3:0] OPCOde
);

  wire Clock_out;
  wire [1:0] bit_extender_2_out;
  wire [3:0] multiplexer_1_out;
  wire [15:0] adder_1_out, bit_extender_1_out, multiplexer_2_out, multiplexer_3_out, ram_1_data, register_1_q;

  Register #(.width(16)) register_1 (.D(adder_1_out), .Q(register_1_q), .clk(Clock_out), .clr(Clear_2));  // open: en
  Clock Clock (.out(Clock_out));
  Adder #(.width(16)) adder_1 (.a(register_1_q), .b(16'h1), .out(adder_1_out));  // open: cin, cout
  ROM #(.addrWidth(16), .dataWidth(16)) rom_1 (.addr(register_1_q), .data({OPCOde, RS, RT, RD}));  // open: sel
  Multiplexer #(.width(4), .enable("false")) multiplexer_1 (.in0(RT), .in1(RD), .out(multiplexer_1_out), .sel(R_I));
  assign bit_extender_1_out = {{12{1'b0}}, RD};  // Bit_Extender bit_extender_1
  Bit_Extender #(.in_width(4), .out_width(2)) bit_extender_2 (.in(OPCOde), .out(bit_extender_2_out));
  _16_Bit_Register_File u_16_bit_register_file_1 (
    .Data_Write(multiplexer_3_out), .Enable(R_I_2), .Data_Read_1(out_14), .Data_Read_2(out_11),
    .RD(multiplexer_1_out), .RS(RS), .RT(RT), .Clock(Clock_out));
  _16_Bit_ALU u_16_bit_alu_1 (
    .B(multiplexer_2_out), .A(out_14), .OpCode(bit_extender_2_out), .Cin(Cin), .Result(ALU_Result));  // open: OverFlow, Zero, Cout
  Multiplexer #(.width(16), .enable("false")) multiplexer_2 (
    .in0(out_11), .in1(bit_extender_1_out), .out(multiplexer_2_out), .sel(R_I_3));
  RAM #(.addrWidth(16), .dataWidth(16), .bus("separate")) ram_1 (
    .addr(ALU_Result), .din(out_11), .data(ram_1_data), .str(SW), .sel(Select), .clk(Clock_out), .ld(LW),
    .clr(Clear));
  Multiplexer #(.width(16), .enable("false")) multiplexer_3 (
    .in0(ALU_Result), .in1(ram_1_data), .out(multiplexer_3_out), .sel(in_9));

  // Notes on the sheet:
  //   Instruction Memory
  //   Instruction Fetch
  //   contents of rom_1 (hex, n*v repeats v):
  //   2241
  //   Instruction Decode
  //   Execute
  //   Write Data Line
  //   Access Memory
  //   Memory Access
  //   Write Back
endmodule

module _16_Bit_Register_File (
  input  [15:0] Data_Write,
  input  Clock,
  input  [3:0] RS,
  input  Enable,
  input  [3:0] RD,
  input  [3:0] RT,
  output [15:0] Data_Read_1,
  output [15:0] Data_Read_2
);

  wire demultiplexer_1_out0, demultiplexer_1_out1, demultiplexer_1_out2, demultiplexer_1_out3,
       demultiplexer_1_out4, demultiplexer_1_out5, demultiplexer_1_out6, demultiplexer_1_out7,
       demultiplexer_1_out8, demultiplexer_1_out9, demultiplexer_1_out10, demultiplexer_1_out11,
       demultiplexer_1_out12, demultiplexer_1_out13, demultiplexer_1_out14, demultiplexer_1_out15, Reset_out;
  wire [15:0] register_1_q, register_2_q, register_3_q, register_4_q, register_5_q, register_6_q,
       register_7_q, register_8_q, register_9_q, register_10_q, register_11_q, register_12_q, register_13_q,
       register_14_q, register_15_q, register_16_q;

  Demultiplexer #(.select(4), .enable("false")) demultiplexer_1 (
    .out0(demultiplexer_1_out0), .out1(demultiplexer_1_out1), .out2(demultiplexer_1_out2),
    .out3(demultiplexer_1_out3), .out4(demultiplexer_1_out4), .out5(demultiplexer_1_out5),
    .out6(demultiplexer_1_out6), .out7(demultiplexer_1_out7), .out8(demultiplexer_1_out8),
    .out9(demultiplexer_1_out9), .out10(demultiplexer_1_out10), .out11(demultiplexer_1_out11),
    .out12(demultiplexer_1_out12), .out13(demultiplexer_1_out13), .out14(demultiplexer_1_out14),
    .out15(demultiplexer_1_out15), .in(Enable), .sel(RD));
  Register #(.width(16)) register_1 (
    .D(Data_Write), .en(demultiplexer_1_out0), .Q(register_1_q), .clk(Clock), .clr(Reset_out));
  Register #(.width(16)) register_2 (
    .D(Data_Write), .en(demultiplexer_1_out1), .Q(register_2_q), .clk(Clock), .clr(Reset_out));
  Register #(.width(16)) register_3 (
    .D(Data_Write), .en(demultiplexer_1_out2), .Q(register_3_q), .clk(Clock), .clr(Reset_out));
  Register #(.width(16)) register_4 (
    .D(Data_Write), .en(demultiplexer_1_out3), .Q(register_4_q), .clk(Clock), .clr(Reset_out));
  Register #(.width(16)) register_5 (
    .D(Data_Write), .en(demultiplexer_1_out4), .Q(register_5_q), .clk(Clock), .clr(Reset_out));
  Register #(.width(16)) register_6 (
    .D(Data_Write), .en(demultiplexer_1_out5), .Q(register_6_q), .clk(Clock), .clr(Reset_out));
  Register #(.width(16)) register_7 (
    .D(Data_Write), .en(demultiplexer_1_out6), .Q(register_7_q), .clk(Clock), .clr(Reset_out));
  Register #(.width(16)) register_8 (
    .D(Data_Write), .en(demultiplexer_1_out7), .Q(register_8_q), .clk(Clock), .clr(Reset_out));
  Register #(.width(16)) register_9 (
    .D(Data_Write), .en(demultiplexer_1_out8), .Q(register_9_q), .clk(Clock), .clr(Reset_out));
  Register #(.width(16)) register_10 (
    .D(Data_Write), .en(demultiplexer_1_out9), .Q(register_10_q), .clk(Clock), .clr(Reset_out));
  Register #(.width(16)) register_11 (
    .D(Data_Write), .en(demultiplexer_1_out10), .Q(register_11_q), .clk(Clock), .clr(Reset_out));
  Register #(.width(16)) register_12 (
    .D(Data_Write), .en(demultiplexer_1_out11), .Q(register_12_q), .clk(Clock), .clr(Reset_out));
  Register #(.width(16)) register_13 (
    .D(Data_Write), .en(demultiplexer_1_out12), .Q(register_13_q), .clk(Clock), .clr(Reset_out));
  Register #(.width(16)) register_14 (
    .D(Data_Write), .en(demultiplexer_1_out13), .Q(register_14_q), .clk(Clock), .clr(Reset_out));
  Register #(.width(16)) register_15 (
    .D(Data_Write), .en(demultiplexer_1_out14), .Q(register_15_q), .clk(Clock), .clr(Reset_out));
  Register #(.width(16)) register_16 (
    .D(Data_Write), .en(demultiplexer_1_out15), .Q(register_16_q), .clk(Clock), .clr(Reset_out));
  Button Reset (.out(Reset_out));
  Multiplexer #(.select(4), .width(16), .enable("false")) multiplexer_1 (
    .in0(register_1_q), .in1(register_2_q), .in2(register_3_q), .in3(register_4_q), .in4(register_5_q),
    .in5(register_6_q), .in6(register_7_q), .in7(register_8_q), .in8(register_9_q), .in9(register_10_q),
    .in10(register_11_q), .in11(register_12_q), .in12(register_13_q), .in13(register_14_q),
    .in14(register_15_q), .in15(register_16_q), .out(Data_Read_1), .sel(RS));
  Multiplexer #(.select(4), .width(16), .enable("false")) multiplexer_2 (
    .in0(register_1_q), .in1(register_2_q), .in2(register_3_q), .in3(register_4_q), .in4(register_5_q),
    .in5(register_6_q), .in6(register_7_q), .in7(register_8_q), .in8(register_9_q), .in9(register_10_q),
    .in10(register_11_q), .in11(register_12_q), .in12(register_13_q), .in13(register_14_q),
    .in14(register_15_q), .in15(register_16_q), .out(Data_Read_2), .sel(RT));
endmodule

module _1_Bit_ALU (
  input  B,
  input  A,
  input  Cin,
  input  [1:0] OpCode,
  output Overflow,
  output Output,
  output Zero,
  output Cout
);

  wire adder_1_out, and_1_out, or_1_out, subtractor_1_out;

  and and_1 (and_1_out, A, B);
  or or_1 (or_1_out, A, B);
  Adder #(.width(1)) adder_1 (.a(A), .b(B), .out(adder_1_out), .cin(Cin), .cout(Cout));
  Subtractor #(.width(1)) subtractor_1 (.a(A), .b(B), .out(subtractor_1_out));  // open: bin, bout
  Multiplexer #(.select(2), .enable("false")) multiplexer_1 (
    .in0(and_1_out), .in1(or_1_out), .in2(adder_1_out), .in3(subtractor_1_out), .out(Output), .sel(OpCode));
  xor xor_1 (Overflow, Output, Cout);
  nor nor_1 (Zero, Output, Cout);
endmodule

module _16_Bit_ALU (
  input  [15:0] B,
  input  [15:0] A,
  input  [1:0] OpCode,
  input  Cin,
  output [15:0] Result,
  output [15:0] OverFlow,
  output [15:0] Zero,
  output Cout
);

  wire n1_bit_alu_1_cout, n1_bit_alu_2_cout, n1_bit_alu_3_cout, n1_bit_alu_4_cout, n1_bit_alu_5_cout,
       n1_bit_alu_6_cout, n1_bit_alu_7_cout, n1_bit_alu_8_cout, n1_bit_alu_9_cout, n1_bit_alu_10_cout,
       n1_bit_alu_11_cout, n1_bit_alu_12_cout, n1_bit_alu_13_cout, n1_bit_alu_14_cout, n1_bit_alu_15_cout;

  _1_Bit_ALU u_1_bit_alu_1 (
    .Overflow(OverFlow[0]), .Output(Result[0]), .Zero(Zero[0]), .Cout(n1_bit_alu_1_cout), .B(B[0]), .A(A[0]),
    .Cin(Cin), .OpCode(OpCode));
  _1_Bit_ALU u_1_bit_alu_2 (
    .Overflow(OverFlow[1]), .Output(Result[1]), .Zero(Zero[1]), .Cout(n1_bit_alu_2_cout), .B(B[1]), .A(A[1]),
    .Cin(n1_bit_alu_1_cout), .OpCode(OpCode));
  _1_Bit_ALU u_1_bit_alu_3 (
    .Overflow(OverFlow[2]), .Output(Result[2]), .Zero(Zero[2]), .Cout(n1_bit_alu_3_cout), .B(B[2]), .A(A[2]),
    .Cin(n1_bit_alu_2_cout), .OpCode(OpCode));
  _1_Bit_ALU u_1_bit_alu_4 (
    .Overflow(OverFlow[3]), .Output(Result[3]), .Zero(Zero[3]), .Cout(n1_bit_alu_4_cout), .B(B[3]), .A(A[3]),
    .Cin(n1_bit_alu_3_cout), .OpCode(OpCode));
  _1_Bit_ALU u_1_bit_alu_5 (
    .Overflow(OverFlow[4]), .Output(Result[4]), .Zero(Zero[4]), .Cout(n1_bit_alu_5_cout), .B(B[4]), .A(A[4]),
    .Cin(n1_bit_alu_4_cout), .OpCode(OpCode));
  _1_Bit_ALU u_1_bit_alu_6 (
    .Overflow(OverFlow[5]), .Output(Result[5]), .Zero(Zero[5]), .Cout(n1_bit_alu_6_cout), .B(B[5]), .A(A[5]),
    .Cin(n1_bit_alu_5_cout), .OpCode(OpCode));
  _1_Bit_ALU u_1_bit_alu_7 (
    .Overflow(OverFlow[6]), .Output(Result[6]), .Zero(Zero[6]), .Cout(n1_bit_alu_7_cout), .B(B[6]), .A(A[6]),
    .Cin(n1_bit_alu_6_cout), .OpCode(OpCode));
  _1_Bit_ALU u_1_bit_alu_8 (
    .Overflow(OverFlow[7]), .Output(Result[7]), .Zero(Zero[7]), .Cout(n1_bit_alu_8_cout), .B(B[7]), .A(A[7]),
    .Cin(n1_bit_alu_7_cout), .OpCode(OpCode));
  _1_Bit_ALU u_1_bit_alu_9 (
    .Overflow(OverFlow[8]), .Output(Result[8]), .Zero(Zero[8]), .Cout(n1_bit_alu_9_cout), .B(B[8]), .A(A[8]),
    .Cin(n1_bit_alu_8_cout), .OpCode(OpCode));
  _1_Bit_ALU u_1_bit_alu_10 (
    .Overflow(OverFlow[9]), .Output(Result[9]), .Zero(Zero[9]), .Cout(n1_bit_alu_10_cout), .B(B[9]),
    .A(A[9]), .Cin(n1_bit_alu_9_cout), .OpCode(OpCode));
  _1_Bit_ALU u_1_bit_alu_11 (
    .Overflow(OverFlow[10]), .Output(Result[10]), .Zero(Zero[10]), .Cout(n1_bit_alu_11_cout), .B(B[10]),
    .A(A[10]), .Cin(n1_bit_alu_10_cout), .OpCode(OpCode));
  _1_Bit_ALU u_1_bit_alu_12 (
    .Overflow(OverFlow[11]), .Output(Result[11]), .Zero(Zero[11]), .Cout(n1_bit_alu_12_cout), .B(B[11]),
    .A(A[11]), .Cin(n1_bit_alu_11_cout), .OpCode(OpCode));
  _1_Bit_ALU u_1_bit_alu_13 (
    .Overflow(OverFlow[12]), .Output(Result[12]), .Zero(Zero[12]), .Cout(n1_bit_alu_13_cout), .B(B[12]),
    .A(A[12]), .Cin(n1_bit_alu_12_cout), .OpCode(OpCode));
  _1_Bit_ALU u_1_bit_alu_14 (
    .Overflow(OverFlow[13]), .Output(Result[13]), .Zero(Zero[13]), .Cout(n1_bit_alu_14_cout), .B(B[13]),
    .A(A[13]), .Cin(n1_bit_alu_13_cout), .OpCode(OpCode));
  _1_Bit_ALU u_1_bit_alu_15 (
    .Overflow(OverFlow[14]), .Output(Result[14]), .Zero(Zero[14]), .Cout(n1_bit_alu_15_cout), .B(B[14]),
    .A(A[14]), .Cin(n1_bit_alu_14_cout), .OpCode(OpCode));
  _1_Bit_ALU u_1_bit_alu_16 (
    .Overflow(OverFlow[15]), .Output(Result[15]), .Zero(Zero[15]), .Cout(Cout), .B(B[15]), .A(A[15]),
    .Cin(n1_bit_alu_15_cout), .OpCode(OpCode));
endmodule
