// Logisim project Lab 02 [ 4 bit arithmetic unit ].circ as structural Verilog: 1 circuit, main circuit main
module main (
  input  Cin,
  input  A0,
  input  B0,
  input  [1:0] S1_S0,
  input  A1,
  input  B1,
  input  A2,
  input  B2,
  input  A3,
  input  B3,
  input  Y,
  output out_12,
  output out_13,
  output [3:0] Ouput,
  output out_15,
  output out_16,
  output Cout
);

  wire adder_1_cout, adder_2_cout, adder_3_cout, multiplexer_1_out, multiplexer_2_out, multiplexer_3_out,
       multiplexer_4_out, not_1_out, not_2_out, not_3_out, not_4_out, not_5_out;

  not not_1 (not_1_out, B0);
  not not_2 (not_2_out, B1);
  not not_3 (not_3_out, B2);
  not not_4 (not_4_out, B3);
  not not_5 (not_5_out, Y);
  Multiplexer #(.select(2), .enable("false")) multiplexer_1 (
    .in0(B0), .in1(not_1_out), .in2(Y), .in3(not_5_out), .out(multiplexer_1_out), .sel(S1_S0));
  Multiplexer #(.select(2), .enable("false")) multiplexer_2 (
    .in0(B1), .in1(not_2_out), .in2(Y), .in3(not_5_out), .out(multiplexer_2_out), .sel(S1_S0));
  Multiplexer #(.select(2), .enable("false")) multiplexer_3 (
    .in0(B2), .in1(not_3_out), .in2(Y), .in3(not_5_out), .out(multiplexer_3_out), .sel(S1_S0));
  Multiplexer #(.select(2), .enable("false")) multiplexer_4 (
    .in0(B3), .in1(not_4_out), .in2(Y), .in3(not_5_out), .out(multiplexer_4_out), .sel(S1_S0));
  Adder #(.width(1)) adder_1 (.a(A0), .b(multiplexer_1_out), .out(Ouput[0]), .cin(Cin), .cout(adder_1_cout));
  Adder #(.width(1)) adder_2 (.a(A1), .b(multiplexer_2_out), .out(Ouput[1]), .cin(adder_1_cout), .cout(adder_2_cout));
  Adder #(.width(1)) adder_3 (.a(A2), .b(multiplexer_3_out), .out(Ouput[2]), .cin(adder_2_cout), .cout(adder_3_cout));
  Adder #(.width(1)) adder_4 (.a(A3), .b(multiplexer_4_out), .out(Ouput[3]), .cin(adder_3_cout), .cout(Cout));

  assign out_12 = Ouput[0];
  assign out_13 = Ouput[1];
  assign out_15 = Ouput[2];
  assign out_16 = Ouput[3];
endmodule
