// Logisim project Lab 03 [ 4x3 Multiplier ].circ as structural Verilog: 2 circuits, main circuit main
module main (
  input  A3,
  input  A2,
  input  A1,
  input  A0,
  input  B2,
  input  B1,
  input  B0,
  output out_8
);

  // AND_Gate and_1 has open pins: in0=A3, in1=B2, out=open
  // AND_Gate and_2 has open pins: in0=B2, in1=A2, out=open
  // AND_Gate and_3 has open pins: in0=B1, in1=A3, out=open
  // AND_Gate and_4 has open pins: in0=B2, in1=A1, out=open
  // AND_Gate and_5 has open pins: in0=B1, in1=A2, out=open
  // AND_Gate and_6 has open pins: in0=B0, in1=A3, out=open
  // AND_Gate and_7 has open pins: in0=B2, in1=A0, out=open
  // AND_Gate and_8 has open pins: in0=B1, in1=A1, out=open
  // AND_Gate and_9 has open pins: in0=A2, in1=B0, out=open
  // AND_Gate and_10 has open pins: in0=A0, in1=B1, out=open
  // AND_Gate and_11 has open pins: in0=B0, in1=A1, out=open
  and and_12 (out_8, A0, B0);
endmodule

module _3_bit_Full_Adder (
  input  Cin,
  input  A0,
  input  B0,
  input  A1,
  input  B1,
  input  A2,
  input  B2,
  output C0,
  output C1,
  output C2,
  output Cout
);

  wire adder_1_cout, adder_2_cout;

  Adder #(.width(1)) adder_1 (.a(A0), .b(B0), .out(C0), .cin(Cin), .cout(adder_1_cout));
  Adder #(.width(1)) adder_2 (.a(A1), .b(B1), .out(C1), .cin(adder_1_cout), .cout(adder_2_cout));
  Adder #(.width(1)) adder_3 (.a(A2), .b(B2), .out(C2), .cin(adder_2_cout), .cout(Cout));
endmodule
