// Logisim project Lab 04 [ 4 Bit USR ].circ as structural Verilog: 1 circuit, main circuit main
module main (
  input  [1:0] S1_S0,
  input  SHR,
  input  I0,
  input  I1,
  input  I2,
  input  SHL,
  input  I3,
  output A0,
  output A1,
  output A2,
  output A3
);

  wire Clock_out, multiplexer_1_out, multiplexer_2_out, multiplexer_3_out, multiplexer_4_out, Reset_out;

  Clock Clock (.out(Clock_out));
  Button Reset (.out(Reset_out));
  D_Flip_Flop d_ff_1 (.clk(Clock_out), .D(multiplexer_1_out), .Q(A0), .reset(Reset_out));  // open: Qn, preset, en
  Multiplexer #(.select(2), .enable("false")) multiplexer_1 (
    .in0(A0), .in1(SHR), .in2(A1), .in3(I0), .out(multiplexer_1_out), .sel(S1_S0));
  D_Flip_Flop d_ff_2 (.clk(Clock_out), .D(multiplexer_2_out), .Q(A1), .reset(Reset_out));  // open: Qn, preset, en
  Multiplexer #(.select(2), .enable("false")) multiplexer_2 (
    .in0(A1), .in1(A0), .in2(A2), .in3(I1), .out(multiplexer_2_out), .sel(S1_S0));
  D_Flip_Flop d_ff_3 (.clk(Clock_out), .D(multiplexer_3_out), .Q(A2), .reset(Reset_out));  // open: Qn, preset, en
  Multiplexer #(.select(2), .enable("false")) multiplexer_3 (
    .in0(A2), .in1(A1), .in2(A3), .in3(I2), .out(multiplexer_3_out), .sel(S1_S0));
  D_Flip_Flop d_ff_4 (.clk(Clock_out), .D(multiplexer_4_out), .Q(A3), .reset(Reset_out));  // open: Qn, preset, en
  Multiplexer #(.select(2), .enable("false")) multiplexer_4 (
    .in0(A3), .in1(A2), .in2(SHL), .in3(I3), .out(multiplexer_4_out), .sel(S1_S0));
endmodule
