// Logisim project Lab 05 [ 3 bit up down counter ].circ as structural Verilog: 1 circuit, main circuit main
module main (
  input  M,
  input  in_2,
  input  Enable,
  output out_4,
  output out_5,
  output out_6
);

  wire and_1_out, and_2_out, Clock_out, not_1_out, or_1_out, Reset_out, TB_qn, TC_qn, xor_1_out;

  not not_1 (not_1_out, M);
  and and_1 (and_1_out, M, TB_qn, TC_qn);
  and and_2 (and_2_out, not_1_out, out_5, out_6);
  xor xor_1 (xor_1_out, M, out_6);
  or or_1 (or_1_out, and_1_out, and_2_out);
  T_Flip_Flop TA (.clk(Clock_out), .T(or_1_out), .Q(out_4), .reset(Reset_out), .en(Enable));  // open: Qn, preset
  T_Flip_Flop TB (
    .clk(Clock_out), .T(xor_1_out), .Q(out_5), .Qn(TB_qn), .reset(Reset_out), .en(Enable));  // open: preset
  T_Flip_Flop TC (.clk(Clock_out), .T(in_2), .Q(out_6), .Qn(TC_qn), .reset(Reset_out), .en(Enable));  // open: preset
  Clock Clock (.out(Clock_out));
  Button Reset (.out(Reset_out));
endmodule
