// Logisim project Lab 4.circ as structural Verilog: 1 circuit, main circuit main
module main (
  input  [1:0] S1_S0,
  input  I0,
  input  SHIFT_RIGHT,
  input  I1,
  input  I2,
  input  I3,
  input  SHIFT_LEFT,
  output A0,
  output A1,
  output A2,
  output A3
);

  wire CLEAR_out, clock_1_out, multiplexer_1_out, multiplexer_2_out, multiplexer_3_out, multiplexer_4_out;

  Clock clock_1 (.out(clock_1_out));
  Button CLEAR (.out(CLEAR_out));
  D_Flip_Flop d_ff_1 (.clk(clock_1_out), .D(multiplexer_1_out), .Q(A0), .reset(CLEAR_out));  // open: Qn, preset, en
  Multiplexer #(.select(2), .enable("false")) multiplexer_1 (
    .in0(A1), .in1(I0), .in2(SHIFT_RIGHT), .in3(A0), .out(multiplexer_1_out), .sel(S1_S0));
  Multiplexer #(.select(2), .enable("false")) multiplexer_2 (
    .in0(A2), .in1(I1), .in2(A0), .in3(A1), .out(multiplexer_2_out), .sel(S1_S0));
  D_Flip_Flop d_ff_2 (.clk(clock_1_out), .D(multiplexer_2_out), .Q(A1), .reset(CLEAR_out));  // open: Qn, preset, en
  D_Flip_Flop d_ff_3 (.clk(clock_1_out), .D(multiplexer_3_out), .Q(A2), .reset(CLEAR_out));  // open: Qn, preset, en
  Multiplexer #(.select(2), .enable("false")) multiplexer_3 (
    .in0(A3), .in1(I2), .in2(A1), .in3(A2), .out(multiplexer_3_out), .sel(S1_S0));
  Multiplexer #(.select(2), .enable("false")) multiplexer_4 (
    .in0(SHIFT_LEFT), .in1(I3), .in2(A2), .in3(A3), .out(multiplexer_4_out), .sel(S1_S0));
  D_Flip_Flop d_ff_4 (.clk(clock_1_out), .D(multiplexer_4_out), .Q(A3), .reset(CLEAR_out));  // open: Qn, preset, en

  // Notes on the sheet:
  //   00 SHIFT LEFT
  //   10 SHIFT RIGHT
  //   11 NO CHANGE
  //   01 PARALLEL LOAD
endmodule
