// Logisim project Lab Mid.circ as structural Verilog: 1 circuit, main circuit main
module main (
  input  A4,
  input  A3,
  input  A2,
  input  A1,
  input  A0,
  input  B2,
  input  B1,
  input  B0,
  input  in_9,
  output S7,
  output S6,
  output S5,
  output S4,
  output S3,
  output S2,
  output S1,
  output S0
);

  wire adder_2_cout, adder_3_cout, adder_4_cout, adder_4_out, adder_5_cout, adder_6_cout, adder_6_out,
       adder_7_cout, adder_8_cout, adder_8_out, adder_9_cout, and_1_out, and_2_out, and_3_out, and_4_out,
       and_5_out, and_6_out, and_7_out, and_8_out, and_9_out, and_10_out, and_11_out, and_12_out, and_13_out,
       and_14_out;

  Adder #(.width(1)) adder_1 (.a(and_1_out), .b(in_9), .out(S6), .cin(adder_2_cout), .cout(S7));
  and and_1 (and_1_out, A4, B2);
  and and_2 (and_2_out, A4, B1);
  Adder #(.width(1)) adder_2 (.a(and_2_out), .b(and_4_out), .out(S5), .cin(adder_3_cout), .cout(adder_2_cout));
  and and_3 (and_3_out, A4, B0);
  Adder #(.width(1)) adder_3 (.a(adder_4_out), .b(and_8_out), .out(S4), .cin(adder_4_cout), .cout(adder_3_cout));
  and and_4 (and_4_out, A3, B2);
  and and_5 (and_5_out, A3, B1);
  Adder #(.width(1)) adder_4 (.a(and_3_out), .b(and_5_out), .out(adder_4_out), .cin(adder_5_cout), .cout(adder_4_cout));
  and and_6 (and_6_out, A3, B0);
  and and_7 (and_7_out, A2, B1);
  and and_8 (and_8_out, A2, B2);
  Adder #(.width(1)) adder_5 (.a(adder_6_out), .b(and_11_out), .out(S3), .cin(adder_6_cout), .cout(adder_5_cout));
  and and_9 (and_9_out, A2, B0);
  Adder #(.width(1)) adder_6 (.a(and_6_out), .b(and_7_out), .out(adder_6_out), .cin(adder_7_cout), .cout(adder_6_cout));
  and and_10 (and_10_out, A1, B1);
  and and_11 (and_11_out, A1, B2);
  Adder #(.width(1)) adder_7 (.a(adder_8_out), .b(and_14_out), .out(S2), .cin(adder_8_cout), .cout(adder_7_cout));
  and and_12 (and_12_out, A1, B0);
  Adder #(.width(1)) adder_8 (
    .a(and_9_out), .b(and_10_out), .out(adder_8_out), .cin(adder_9_cout), .cout(adder_8_cout));
  and and_13 (and_13_out, A0, B1);
  and and_14 (and_14_out, A0, B2);
  Adder #(.width(1)) adder_9 (.a(and_13_out), .b(and_12_out), .out(S1), .cin(in_9), .cout(adder_9_cout));
  and and_15 (S0, A0, B0);
endmodule
